// Logisim project cpu.circ as structural Verilog: 16 circuits, main circuit S8BC
module S8BC (
  input  Rst
);

  wire and_1_out, Clk_out, csd_1_db_ir, csd_1_iend, HLT, jsd_1_weo, not_1_out, or_1_out, sr_1_fo, undriven_2;
  wire [1:0] csd_1_dl_lo, csd_1_mem_db;
  wire [2:0] csd_1_db_arl, sc_1_out_3, undriven, undriven_4;
  wire [3:0] undriven_3;
  wire [4:0] csd_1_pc_en;
  wire [7:0] a_1_ro, alu_1_ao, alu_1_ro, ar_1_adho, ar_1_adlo, dp_1_adho, dp_1_adlo, ir_1_do, memory_1_do;
  wire [10:0] csd_1_ab_dp;

  LED u_Hlt (.in(HLT));
  Clock Clk (.out(Clk_out));
  not not_1 (not_1_out, HLT);
  and and_1 (and_1_out, Clk_out, not_1_out);
  IR ir_1 (.DO(ir_1_do), .WE(csd_1_db_ir), .DI(memory_1_do), .Clk(and_1_out), .Reset(Rst));
  SC sc_1 (.out_3(sc_1_out_3), .Clk(and_1_out), .Rst(or_1_out));
  CSD csd_1 (
    .IEnd(csd_1_iend), .DB_IR(csd_1_db_ir), .DB_Mem(csd_1_mem_db[1]), .Mem_DB(csd_1_mem_db[0]),
    .AB_DP(csd_1_ab_dp[0]), .DB_ARL(csd_1_db_arl[0]), .DB_ARH(csd_1_db_arl[1]), .AR_AB(csd_1_db_arl[2]),
    .AB_PC(csd_1_ab_dp[4]), .PC_En(csd_1_pc_en[0]), .PCL_ABL(csd_1_pc_en[1]), .PCH_ABH(csd_1_pc_en[2]),
    .PCL_DB(csd_1_pc_en[3]), .PCH_DB(csd_1_pc_en[4]), .JE_Inv(csd_1_ab_dp[10]), .DL_Lo(csd_1_dl_lo[0]),
    .DL_Hi(csd_1_dl_lo[1]), .Opcode(ir_1_do), .Step(sc_1_out_3));  // open: Y_DB, DB_SR, SR_DB, HF_Set, DB_R, R_DB, ALU_R, ALU_A, DB_A, A_DB, SP_Inc, SP_Dec, DB_SP, SP_DB, SP_AB, DB_X, X_DB, DB_Y, SR_Sel, ALU_Sel
  or or_1 (or_1_out, undriven_2, Rst);
  Memory memory_1 (
    .DO(memory_1_do), .WE(csd_1_mem_db[1]), .Clk(and_1_out), .DI(memory_1_do), .ADL(dp_1_adlo),
    .ADH(dp_1_adho), .OE(csd_1_mem_db[0]));
  ALU alu_1 (.RO(alu_1_ro), .AO(alu_1_ao), .DBI(memory_1_do), .AI(a_1_ro), .OpS(undriven_3));  // open: C, Z
  // Probe on undriven_3
  // Probe on memory_1_do
  R r_1 (.out_8(memory_1_do), .DBI(memory_1_do), .RI(alu_1_ro), .Clk(and_1_out), .Rst(Rst));  // open: RWE, DWE, OE
  A a_1 (
    .DBO(memory_1_do), .RO(a_1_ro), .DBI(memory_1_do), .RI(alu_1_ao), .RWE(undriven[0]), .DWE(undriven[1]),
    .Clk(and_1_out), .Rst(Rst), .DOE(undriven[2]));
  DP dp_1 (
    .ADLO(dp_1_adlo), .ADHO(dp_1_adho), .ADLI(ar_1_adlo), .ADHI(ar_1_adho), .WE(csd_1_ab_dp[0]),
    .Clk(and_1_out), .Rst(Rst));
  AR ar_1 (
    .ADLO(ar_1_adlo), .ADHO(ar_1_adho), .LWE(csd_1_db_arl[0]), .HWE(csd_1_db_arl[1]), .ADLI(memory_1_do),
    .Clk(and_1_out), .Rst(Rst), .OE(csd_1_db_arl[2]));
  PC pc_1 (
    .ABLO(ar_1_adlo), .ABHO(ar_1_adho), .DB(memory_1_do), .Reset(Rst), .ABWE(jsd_1_weo), .CE(csd_1_pc_en[0]),
    .Clk(and_1_out), .ABLI(ar_1_adlo), .ABHI(ar_1_adho), .ALOE(csd_1_pc_en[1]), .AHOE(csd_1_pc_en[2]),
    .DLOE(csd_1_pc_en[3]), .DHOE(csd_1_pc_en[4]));
  XY xy_1 (.DBO(memory_1_do), .DBI(memory_1_do), .Clk(and_1_out), .Reset(Rst));  // open: XWE, YWE, XOE, YOE
  // Probe on ar_1_adlo
  // Probe on ar_1_adho
  Latch latch_1 (
    .DBO(memory_1_do), .ADLO(ar_1_adlo), .ADHO(ar_1_adho), .DBI(memory_1_do), .CL(csd_1_dl_lo[0]),
    .CH(csd_1_dl_lo[1]), .ADLI(ar_1_adlo), .ADHI(ar_1_adho));
  SP sp_1 (
    .AHO(ar_1_adho), .ALO(ar_1_adlo), .DO(memory_1_do), .DI(memory_1_do), .Clk(and_1_out), .Rst(Rst));  // open: WE, IE, DE, AOE, DOE
  JSD jsd_1 (.WEO(jsd_1_weo), .WEI(csd_1_ab_dp[4]), .JE(sr_1_fo), .Inv(csd_1_ab_dp[10]));
  SR sr_1 (
    .FO(sr_1_fo), .HO(HLT), .DO(memory_1_do), .DI(memory_1_do), .Clk(and_1_out), .Rst(Rst), .FS(undriven_4));  // open: IO, OE, WE
  Pull_Resistor pull_resistor_1 (.node(HLT));
  // Probe on undriven_4
endmodule

module PC (
  input  Reset,
  input  ABWE,
  input  CE,
  input  ALOE,
  input  Clk,
  input  AHOE,
  input  [7:0] ABLI,
  input  [7:0] ABHI,
  input  DLOE,
  input  DHOE,
  output [7:0] ABLO,
  output [7:0] ABHO,
  output [7:0] DB
);

  wire or_1_out;
  wire [7:0] multiplexer_1_out;
  wire [15:0] counter_1_q;

  Counter #(.max('hffff), .trigger("falling"), .width(16)) counter_1 (
    .clr(Reset), .load(ABWE), .up(1'b1), .count(CE), .clk(Clk), .D({ABHI, ABLI}), .Q(counter_1_q));  // open: carry
  assign ABLO = ALOE ? counter_1_q[7:0] : 8'bz;  // Controlled_Buffer controlled_buffer_1
  assign ABHO = AHOE ? counter_1_q[15:8] : 8'bz;  // Controlled_Buffer controlled_buffer_2
  or or_1 (or_1_out, DHOE, DLOE);
  Multiplexer #(.width(8)) multiplexer_1 (
    .in0(counter_1_q[7:0]), .in1(counter_1_q[15:8]), .out(multiplexer_1_out), .sel(DHOE));
  assign DB = or_1_out ? multiplexer_1_out : 8'bz;  // Controlled_Buffer controlled_buffer_3
endmodule

module Memory (
  input  WE,
  input  Clk,
  input  [7:0] DI,
  input  OE,
  input  [7:0] ADL,
  input  [7:0] ADH,
  output [7:0] DO
);

  wire and_1_out, not_1_out, not_2_out;
  wire [7:0] controlled_buffer_1_out, ram_1_dout, rom_1_data;

  not not_1 (not_1_out, ADH[7]);
  RAM #(.addrWidth(15)) ram_1 (
    .addr({ADH[6:0], ADL}), .we(and_1_out), .oe(1'b1), .clk(Clk), .din(DI), .dout(ram_1_dout));
  and and_1 (and_1_out, WE, not_1_out);
  ROM #(.addrWidth(15)) rom_1 (.addr({ADH[6:0], ADL}), .data(rom_1_data));
  assign controlled_buffer_1_out = not_2_out ? ram_1_dout : 8'bz;  // Controlled_Buffer controlled_buffer_1
  not not_2 (not_2_out, ADH[7]);
  assign controlled_buffer_1_out = ADH[7] ? rom_1_data : 8'bz;  // Controlled_Buffer controlled_buffer_2
  assign DO = OE ? controlled_buffer_1_out : 8'bz;  // Controlled_Buffer controlled_buffer_3
endmodule

module XY (
  input  Clk,
  input  Reset,
  input  [7:0] DBI,
  input  XOE,
  input  XWE,
  input  YOE,
  input  YWE,
  output [7:0] DBO
);

  wire [7:0] register_1_q, register_2_q;

  Register register_1 (.D(DBI), .en(XWE), .clk(Clk), .Q(register_1_q), .clr(Reset));
  Register register_2 (.D(DBI), .en(YWE), .clk(Clk), .Q(register_2_q), .clr(Reset));
  assign DBO = XOE ? register_1_q : 8'bz;  // Controlled_Buffer controlled_buffer_1
  assign DBO = YOE ? register_2_q : 8'bz;  // Controlled_Buffer controlled_buffer_2
endmodule

module CSD (
  input  [7:0] Opcode,
  input  [2:0] Step,
  output DB_IR,
  output DB_Mem,
  output Mem_DB,
  output AB_DP,
  output DB_ARL,
  output DB_ARH,
  output AR_AB,
  output AB_PC,
  output PC_En,
  output PCL_ABL,
  output PCH_ABH,
  output PCL_DB,
  output PCH_DB,
  output JE_Inv,
  output DL_Lo,
  output DL_Hi,
  output DB_R,
  output R_DB,
  output ALU_R,
  output [3:0] ALU_Sel,
  output ALU_A,
  output DB_A,
  output A_DB,
  output SP_Inc,
  output SP_Dec,
  output DB_SP,
  output SP_DB,
  output SP_AB,
  output DB_X,
  output X_DB,
  output DB_Y,
  output Y_DB,
  output DB_SR,
  output SR_DB,
  output [2:0] SR_Sel,
  output HF_Set,
  output IEnd
);

  ROM #(.addrWidth(11), .dataWidth(42)) rom_1 (
    .addr({Opcode, Step}),
    .data({IEnd, HF_Set, SR_Sel, SR_DB, DB_SR, Y_DB, DB_Y, X_DB, DB_X, SP_AB, SP_DB, DB_SP, SP_Dec, SP_Inc, A_DB, DB_A, ALU_A, ALU_Sel, ALU_R, R_DB, DB_R, DL_Hi, DL_Lo, JE_Inv, PCH_DB, PCL_DB, PCH_ABH, PCL_ABL, PC_En, AB_PC, AR_AB, DB_ARH, DB_ARL, AB_DP, Mem_DB, DB_Mem, DB_IR}));

  // Notes on the sheet:
  //   contents of rom_1 (hex, n*v repeats v):
  //   70d 20000000000 6*0 70d 100070c 20000000000 5*0 70d 100004408 1000004 20000000000 4*0 70d 400004408
  //   1000004 20000000000 4*0 70d 71c 72c 100004c 20000000000 0 0 0 70d 8000070c 20000000000 5*0 70d
  //   400004408 80000004 20000000000 4*0 70d 71c 72c 8000004c 20000000000 0 0 0 70d 20000070c 20000000000
  //   5*0 70d 100004408 200000004 20000000000 4*0 70d 71c 72c 20000004c 20000000000 0 0 0 70d 0
  //   20000000000 5*0 70d 100004408 2000002 20000000000 4*0 70d 400004408 2000002 20000000000 4*0 70d 71c
  //   72c 200004a 20000000000 0 0 0 70d 71c 72c 10000004a 20000000000 0 0 0 70d 71c 72c 40000004a
  //   20000000000 0 0 0 70d 0 20000000000 5*0 70d 82000000 20000000000 5*0 70d 202000000 20000000000 5*0
  //   70d 101000000 20000000000 5*0 70d 401000000 20000000000 5*0 70d 2010000 101000000 80020000
  //   20000000000 0 0 0 70d 2010000 401000000 200020000 20000000000 0 0 0 70d 100010000 480000000
  //   200020000 20000000000 0 0 0 70d a0000000 20000000000 5*0 70d 110000000 20000000000 5*0 70d 0
  //   20000000000 5*0 70d 8000000 4200000a 20000000000 4*0 70d 8000000 14000000a 20000000000 4*0 70d
  //   8000000 44000000a 20000000000 4*0 70d 4100000c 20000000000 5*0 70d 4500000c 20000000000 5*0 70d
  //   c400000c 20000000000 5*0 70d 24400000c 20000000000 5*0 70d 0 20000000000 5*0 70d 0 20000000000 5*0
  //   70d 0 20000000000 5*0 70d 0 20000000000 5*0 70d 0 20000000000 5*0 70d 0 20000000000 5*0 70d 0
  //   20000000000 5*0 70d 0 20000000000 5*0 70d 0 20000000000 5*0 70d 0 20000000000 5*0 70d 0 20000000000
  //   5*0 70d 0 20000000000 5*0 70d 0 20000000000 5*0 70d 0 20000000000 5*0 70d 0 20000000000 5*0 70d 0
  //   20000000000 5*0 70d 0 20000000000 5*0 70d 0 20000000000 5*0 70d 0 20000000000 5*0 70d 0 20000000000
  //   5*0 70d 0 20000000000 5*0 70d 0 20000000000 5*0 70d 0 20000000000 5*0 70d 0 20000000000 5*0 70d 0
  //   20000000000 5*0 70d 0 20000000000 5*0 70d 0 20000000000 5*0 70d 0 20000000000 5*0 70d 0 20000000000
  //   5*0 70d 0 20000000000 5*0 70d 0 20000000000 5*0 70d 0 20000000000 5*0 70d 0 20000000000 5*0 70d 0
  //   20000000000 5*0 70d 0 20000000000 5*0 70d 0 20000000000 5*0 70d 0 20000000000 5*0 70d 0 20000000000
  //   5*0 70d 0 20000000000 5*0 70d 0 20000000000 5*0 70d 0 20000000000 5*0 70d 0 20000000000 5*0 70d 0
  //   20000000000 5*0 70d 71c 72c c0 20000000000 0 0 0 70d 71c 72c 0 20000000000 0 0 0 70d 71c 72c 0
  //   20000000000 0 0 0 70d 71c 72c 0 20000000000 0 0 0 70d 71c 72c 0 20000000000 0 0 0 70d 71c 72c 0
  //   20000000000 0 0 0 70d 71c 72c 0 20000000000 0 0 0 70d 71c 72c 0 20000000000 0 0 0 70d 71c 72c 0
  //   20000000000 0 0 0 70d 71c 72c 0 20000000000 0 0 0 70d 71c 72c 0 20000000000 0 0 0 70d 8000000
  //   4800100a 4000080a 71c 72c c0 0 70d 4400001c 4400001c c0 20000000000 0 0 0 70d 84400000c 4400001c
  //   4400002c c0 20000000000 0 0 70d 10000000000 20000000000
endmodule

module ALU (
  input  [3:0] OpS,
  input  [7:0] DBI,
  input  [7:0] AI,
  output [7:0] RO,
  output [7:0] AO,
  output C,
  output Z
);

  wire adder_1_cout, adder_2_cout, and_1_out, and_2_out, demultiplexer_1_out1, demultiplexer_1_out2,
       demultiplexer_1_out3, demultiplexer_1_out4, demultiplexer_1_out5, demultiplexer_1_out6,
       demultiplexer_1_out7, demultiplexer_1_out8, demultiplexer_1_out9, demultiplexer_1_out10,
       demultiplexer_1_out11, demultiplexer_1_out12, subtractor_1_bout, subtractor_2_bout;
  wire [7:0] adder_1_out, adder_2_out, and_3_out, divider_1_out, divider_1_rem, multiplier_1_cout,
       multiplier_1_out, not_1_out, or_1_out, shifter_1_out, shifter_2_out, subtractor_1_out,
       subtractor_2_out, xor_1_out;

  assign AO = demultiplexer_1_out1 ? adder_1_out : 8'bz;  // Controlled_Buffer controlled_buffer_1
  Adder adder_1 (.a(AI), .b(DBI), .out(adder_1_out), .cout(adder_1_cout));  // open: cin
  assign C = demultiplexer_1_out1 ? adder_1_cout : 1'bz;  // Controlled_Buffer controlled_buffer_2
  assign AO = demultiplexer_1_out2 ? subtractor_1_out : 8'bz;  // Controlled_Buffer controlled_buffer_3
  Subtractor subtractor_1 (.a(AI), .b(DBI), .out(subtractor_1_out), .bout(subtractor_1_bout));  // open: bin
  assign C = demultiplexer_1_out2 ? subtractor_1_bout : 1'bz;  // Controlled_Buffer controlled_buffer_4
  assign AO = demultiplexer_1_out3 ? multiplier_1_out : 8'bz;  // Controlled_Buffer controlled_buffer_5
  Multiplier multiplier_1 (.a(AI), .b(DBI), .out(multiplier_1_out), .cout(multiplier_1_cout));  // open: cin
  assign AO = demultiplexer_1_out4 ? divider_1_out : 8'bz;  // Controlled_Buffer controlled_buffer_6
  Divider divider_1 (.a(AI), .b(DBI), .out(divider_1_out), .rem(divider_1_rem));  // open: upper
  Demultiplexer #(.select(4)) demultiplexer_1 (
    .out1(demultiplexer_1_out1), .out2(demultiplexer_1_out2), .out3(demultiplexer_1_out3),
    .out4(demultiplexer_1_out4), .out5(demultiplexer_1_out5), .out6(demultiplexer_1_out6),
    .out7(demultiplexer_1_out7), .out8(demultiplexer_1_out8), .out9(demultiplexer_1_out9),
    .out10(demultiplexer_1_out10), .out11(demultiplexer_1_out11), .out12(demultiplexer_1_out12), .in(1'b1),
    .sel(OpS));  // open: out0, out13, out14, out15
  and and_1 (and_1_out, multiplier_1_cout[0], multiplier_1_cout[1], multiplier_1_cout[2], multiplier_1_cout[3], multiplier_1_cout[4], multiplier_1_cout[5], multiplier_1_cout[6], multiplier_1_cout[7]);
  assign C = demultiplexer_1_out3 ? and_1_out : 1'bz;  // Controlled_Buffer controlled_buffer_7
  and and_2 (and_2_out, divider_1_rem[0], divider_1_rem[1], divider_1_rem[2], divider_1_rem[3], divider_1_rem[4], divider_1_rem[5], divider_1_rem[6], divider_1_rem[7]);
  assign C = demultiplexer_1_out4 ? and_2_out : 1'bz;  // Controlled_Buffer controlled_buffer_8
  assign and_3_out = AI & DBI;  // AND_Gate and_3, 8 bits wide
  assign AO = demultiplexer_1_out5 ? and_3_out : 8'bz;  // Controlled_Buffer controlled_buffer_9
  assign or_1_out = AI | DBI;  // OR_Gate or_1, 8 bits wide
  assign AO = demultiplexer_1_out6 ? or_1_out : 8'bz;  // Controlled_Buffer controlled_buffer_10
  assign xor_1_out = AI ^ DBI;  // XOR_Gate xor_1, 8 bits wide
  assign AO = demultiplexer_1_out7 ? xor_1_out : 8'bz;  // Controlled_Buffer controlled_buffer_11
  assign AO = demultiplexer_1_out8 ? shifter_1_out : 8'bz;  // Controlled_Buffer controlled_buffer_12
  Shifter shifter_1 (.in(AI), .\dist (DBI[2:0]), .out(shifter_1_out));
  assign AO = demultiplexer_1_out9 ? shifter_2_out : 8'bz;  // Controlled_Buffer controlled_buffer_13
  Shifter #(.shift("lr")) shifter_2 (.in(AI), .\dist (DBI[2:0]), .out(shifter_2_out));
  assign not_1_out = ~DBI;  // NOT_Gate not_1, 8 bits wide
  assign AO = demultiplexer_1_out10 ? not_1_out : 8'bz;  // Controlled_Buffer controlled_buffer_14
  assign AO = demultiplexer_1_out11 ? adder_2_out : 8'bz;  // Controlled_Buffer controlled_buffer_15
  Adder adder_2 (.a(DBI), .b(8'h1), .out(adder_2_out), .cin(1'b0), .cout(adder_2_cout));
  assign C = demultiplexer_1_out11 ? adder_2_cout : 1'bz;  // Controlled_Buffer controlled_buffer_16
  assign AO = demultiplexer_1_out12 ? subtractor_2_out : 8'bz;  // Controlled_Buffer controlled_buffer_17
  Subtractor subtractor_2 (.a(DBI), .b(8'h1), .out(subtractor_2_out), .bin(1'b0), .bout(subtractor_2_bout));
  assign C = demultiplexer_1_out12 ? subtractor_2_bout : 1'bz;  // Controlled_Buffer controlled_buffer_18
  Pull_Resistor pull_resistor_1 (.node(AO));
  Pull_Resistor pull_resistor_2 (.node(C));
  nor nor_1 (Z, AO[0], AO[1], AO[2], AO[3], AO[4], AO[5], AO[6], AO[7]);

  assign RO = AO;
endmodule

module IR (
  input  [7:0] DI,
  input  WE,
  input  Clk,
  input  Reset,
  output [7:0] DO
);

  Register register_1 (.D(DI), .en(WE), .clk(Clk), .Q(DO), .clr(Reset));
endmodule

module AR (
  input  Clk,
  input  Rst,
  input  OE,
  input  [7:0] ADLI,
  input  LWE,
  input  HWE,
  output [7:0] ADLO,
  output [7:0] ADHO
);

  wire [7:0] register_1_q, register_2_q;

  Register register_1 (.D(ADLI), .en(LWE), .clk(Clk), .Q(register_1_q), .clr(Rst));
  Register register_2 (.D(ADLI), .en(HWE), .clk(Clk), .Q(register_2_q), .clr(Rst));
  assign ADLO = OE ? register_1_q : 8'bz;  // Controlled_Buffer controlled_buffer_1
  assign ADHO = OE ? register_2_q : 8'bz;  // Controlled_Buffer controlled_buffer_2
endmodule

module DP (
  input  Clk,
  input  Rst,
  input  [7:0] ADLI,
  input  [7:0] ADHI,
  input  WE,
  output [7:0] ADLO,
  output [7:0] ADHO
);

  Register #(.width(16)) register_1 (.D({ADHI, ADLI}), .en(WE), .clk(Clk), .Q({ADHO, ADLO}), .clr(Rst));
endmodule

module SP (
  input  IE,
  input  DE,
  input  AOE,
  input  [7:0] DI,
  input  DOE,
  input  WE,
  input  Clk,
  input  Rst,
  output [7:0] AHO,
  output [7:0] ALO,
  output [7:0] DO
);

  wire not_1_out, xor_1_out;
  wire [7:0] counter_1_q;

  not not_1 (not_1_out, DE);
  xor xor_1 (xor_1_out, IE, DE);
  Counter counter_1 (
    .load(WE), .D(DI), .count(xor_1_out), .Q(counter_1_q), .up(not_1_out), .clk(Clk), .clr(Rst));  // open: carry
  assign AHO = AOE ? 8'h1 : 8'bz;  // Controlled_Buffer controlled_buffer_1
  assign ALO = AOE ? counter_1_q : 8'bz;  // Controlled_Buffer controlled_buffer_2
  assign DO = DOE ? counter_1_q : 8'bz;  // Controlled_Buffer controlled_buffer_3
endmodule

module JSD (
  input  WEI,
  input  JE,
  input  Inv,
  output WEO
);

  wire multiplexer_1_out, not_1_out;

  Multiplexer multiplexer_1 (.in0(JE), .in1(not_1_out), .out(multiplexer_1_out), .sel(Inv));
  Pull_Resistor #(.pull(1)) pull_resistor_1 (.node(multiplexer_1_out));
  not not_1 (not_1_out, JE);
  and and_1 (WEO, WEI, multiplexer_1_out);
endmodule

module SR (
  input  [2:0] FS,
  input  OE,
  input  [7:0] DI,
  input  WE,
  input  Clk,
  input  Rst,
  output [7:0] DO,
  output FO,
  output IO,
  output HO
);

  wire demultiplexer_1_out0, demultiplexer_1_out1, demultiplexer_1_out2, demultiplexer_1_out3,
       demultiplexer_1_out4;
  wire [5:0] register_1_q;

  Register register_1 (.D(DI), .en(WE), .clk(Clk), .Q({HO, IO, register_1_q}), .clr(Rst));
  Demultiplexer #(.select(3)) demultiplexer_1 (
    .out0(demultiplexer_1_out0), .out1(demultiplexer_1_out1), .out2(demultiplexer_1_out2),
    .out3(demultiplexer_1_out3), .out4(demultiplexer_1_out4), .in(1'b1), .sel(FS));  // open: out5, out6, out7
  assign FO = demultiplexer_1_out0 ? register_1_q[0] : 1'bz;  // Controlled_Buffer controlled_buffer_1
  assign FO = demultiplexer_1_out1 ? register_1_q[1] : 1'bz;  // Controlled_Buffer controlled_buffer_2
  assign FO = demultiplexer_1_out2 ? register_1_q[2] : 1'bz;  // Controlled_Buffer controlled_buffer_3
  assign FO = demultiplexer_1_out3 ? register_1_q[3] : 1'bz;  // Controlled_Buffer controlled_buffer_4
  assign DO = OE ? {HO, IO, register_1_q} : 8'bz;  // Controlled_Buffer controlled_buffer_5
  assign FO = demultiplexer_1_out4 ? register_1_q[4] : 1'bz;  // Controlled_Buffer controlled_buffer_6
endmodule

module Latch (
  input  CL,
  input  CH,
  input  [7:0] ADLI,
  input  [7:0] DBI,
  input  [7:0] ADHI,
  output [7:0] ADLO,
  output [7:0] DBO,
  output [7:0] ADHO
);

  assign ADLO = CL ? DBI : 8'bz;  // Controlled_Buffer controlled_buffer_1
  assign DBO = CL ? ADLI : 8'bz;  // Controlled_Buffer controlled_buffer_2
  assign DBO = CH ? ADHI : 8'bz;  // Controlled_Buffer controlled_buffer_3
  assign ADHO = CH ? DBI : 8'bz;  // Controlled_Buffer controlled_buffer_4
endmodule

module R (
  input  RWE,
  input  DWE,
  input  OE,
  input  [7:0] DBI,
  input  [7:0] RI,
  input  Clk,
  input  Rst,
  output [7:0] out_8
);

  wire or_1_out;
  wire [7:0] controlled_buffer_1_out, register_1_q;

  assign controlled_buffer_1_out = RWE ? RI : 8'bz;  // Controlled_Buffer controlled_buffer_1
  or or_1 (or_1_out, DWE, RWE);
  Register register_1 (.D(controlled_buffer_1_out), .en(or_1_out), .clk(Clk), .Q(register_1_q), .clr(Rst));
  assign controlled_buffer_1_out = DWE ? DBI : 8'bz;  // Controlled_Buffer controlled_buffer_2
  assign out_8 = OE ? register_1_q : 8'bz;  // Controlled_Buffer controlled_buffer_3
endmodule

module A (
  input  RWE,
  input  DWE,
  input  DOE,
  input  [7:0] DBI,
  input  [7:0] RI,
  input  Clk,
  input  Rst,
  output [7:0] DBO,
  output [7:0] RO
);

  wire or_1_out;
  wire [7:0] controlled_buffer_1_out;

  assign controlled_buffer_1_out = RWE ? RI : 8'bz;  // Controlled_Buffer controlled_buffer_1
  or or_1 (or_1_out, DWE, RWE);
  Register register_1 (.D(controlled_buffer_1_out), .en(or_1_out), .clk(Clk), .Q(RO), .clr(Rst));
  assign controlled_buffer_1_out = DWE ? DBI : 8'bz;  // Controlled_Buffer controlled_buffer_2
  assign DBO = DOE ? RO : 8'bz;  // Controlled_Buffer controlled_buffer_3
endmodule

module SC (
  input  Clk,
  input  Rst,
  output [2:0] out_3
);

  Counter #(.max('h7), .trigger("falling"), .width(3)) counter_1 (
    .load(1'b0), .D(3'b000), .count(1'b1), .Q(out_3), .up(1'b1), .clk(Clk), .clr(Rst));  // open: carry
endmodule
